# Fritzing sketch Prototipação - Projeto 1.1 (saved by Fritzing 0.9.3b)
breadboards: 1

parts:
  R10 = Resistor [tolerance=±5% resistance=720 package=THT]
  R11 = Resistor [tolerance=±5% resistance=720 package=THT]
  R12 = Resistor [tolerance=±5% resistance=720 package=THT]
  R13 = Resistor [tolerance=±5% resistance=720 package=THT]
  R14 = Resistor [tolerance=±5% resistance=720 package=THT]
  R15 = Resistor [tolerance=±5% resistance=720 package=THT]
  R16 = Resistor [tolerance=±5% resistance=720 package=THT]
  R17 = Resistor [tolerance=±5% resistance=720 package=THT]
  R18 = Resistor [tolerance=±5% resistance=720 package=THT]
  LED1 = LED - 5mm [color="Red (633nm)" package="5 mm [THT]"]
  LED2 = LED - 5mm [color="Red (633nm)" package="5 mm [THT]"]
  LED3 = LED - 5mm [color="Red (633nm)" package="5 mm [THT]"]
  LED4 = LED - 5mm [color="Yellow (595nm)" package="5 mm [THT]"]
  LED5 = LED - 5mm [color="Yellow (595nm)" package="5 mm [THT]"]
  LED6 = LED - 5mm [color="Yellow (595nm)" package="5 mm [THT]"]
  LED7 = LED - 5mm [color="Green (555nm)" package="5 mm [THT]"]
  LED9 = LED - 5mm [color="Green (555nm)" package="5 mm [THT]"]
  LED8 = LED - 5mm [color="Green (555nm)" package="5 mm [THT]"]
  Componente1 = Arduino Mega 2560 (Rev3)

nets:
  N1: R10.Pin_0, Componente1.D13_PWM
  N2: R10.Pin_1, LED3.anode
  N3: R11.Pin_0, Componente1.D12_PWM
  N4: R11.Pin_1, LED6.anode
  N5: R12.Pin_0, Componente1.D10_PWM
  N6: R12.Pin_1, LED2.anode
  N7: R13.Pin_0, Componente1.D11_PWM
  N8: R13.Pin_1, LED8.anode
  N9: R14.Pin_0, Componente1.D6_PWM
  N10: R14.Pin_1, LED4.anode
  N11: R15.Pin_0, Componente1.D8_PWM
  N12: R15.Pin_1, LED7.anode
  N13: R16.Pin_1, LED1.anode
  N14: R17.Pin_0, Componente1.D9_PWM
  N15: R17.Pin_1, LED5.anode
  N16: R18.Pin_0, Componente1.D5_PWM
  N17: R18.Pin_1, LED9.anode
  N18: LED1.cathode, LED2.cathode, LED3.cathode, LED4.cathode, LED5.cathode, LED6.cathode, LED7.cathode, LED9.cathode, LED8.cathode, Componente1.GND

// code stored in the sketch: Codigo-Fonte_Projeto1.1.ino

