# Fritzing sketch Prototipação - Projeto 10 (saved by Fritzing 0.9.3b)
breadboards: 1

parts:
  Componente1 = Arduino Uno (Rev3)
  LED1 = LED - 5mm [color="Red (633nm)" package="5 mm [THT]"]
  R1 = Resistor [tolerance=±5% resistance=220 package="0603 [SMD]"]
  KY-1 = Keyes Relay [package=THT]

nets:
  N1: Componente1.D13/SCK, KY-1.signal
  N2: Componente1.GND, KY-1.ground, KY-1.C
  N3: Componente1.5V, R1.Pin_0, KY-1.power
  N4: LED1.cathode, KY-1.NO
  N5: LED1.anode, R1.Pin_1

custom parts:
  Keyes Relay: The Keyes 5V relay module is suitable for SCM development, home appliance control. It uses a 5V~12V TIL control signal which can control DC / AC signal.
