# Fritzing sketch Prototipação - Projeto Final (saved by Fritzing 0.9.3b)
breadboards: 1

parts:
  Componente1 = Arduino Uno (Rev3)
  S1 = Pushbutton [package="[THT]"]
  S2 = Pushbutton [package="[THT]"]
  DHT1 = DHT11 Humitidy and Temperature Sensor
  KY-1 = Keyes Relay [package=THT]
  TCRT1 = TCRT5000 sensor module [part_number=151608]
  Componente2 = LCD1602-I2C
  SG1 = Buzzer 12mm [package=buzzer-12mm-ns]
  LED1 = smd LED [color="Yellow (595nm)" package="0805 [SMD]"]  # not connected
  R3 = Resistor [tolerance=±5% resistance=220 package=THT]
  R5 = Resistor [tolerance=±5% resistance=220 package=THT]

nets:
  N1: Componente1.A4/SDA, Componente2.SDA
  N2: Componente1.A5/SCL, Componente2.SCL
  N3: Componente1.D8, KY-1.ground
  N4: Componente1.D12/MISO, S1.Pin_1, S1.Pin_2, R5.Pin_0
  N5: Componente1.D13/SCK, S2.Pin_1, S2.Pin_2, R3.Pin_0
  GND: Componente1.GND, DHT1.GND, KY-1.power, TCRT1.D-, TCRT1.T-, Componente2.GND, SG1.1
  N6: Componente1.D2, DHT1.DATA
  N7: Componente1.D4, SG1.2
  N8: Componente1.D6_PWM, TCRT1.T+
  5V: Componente1.5V, S1.Pin_3, S1.Pin_4, S2.Pin_3, S2.Pin_4, DHT1.VDD, KY-1.signal, TCRT1.D+, Componente2.VCC
  N9: R3.Pin_1, R5.Pin_1

custom parts:
  DHT11 Humitidy and Temperature Sensor: DHT11 Humidity and Temperature Sensor
  Keyes Relay: The Keyes 5V relay module is suitable for SCM development, home appliance control. It uses a 5V~12V TIL control signal which can control DC / AC signal.
  TCRT5000 sensor module: breakout board with TCRT5000
  LCD1602-I2C: A standard character display, usually with 2x16 characters. Comes in many colors with LCM1602 IIC attached.
