# Fritzing sketch Prototipação - Projetos SOS (saved by Fritzing 0.9.3b)
breadboards: 1

parts:
  Componente1 = Arduino Uno (Rev3)
  LED1 = smd LED [color="Red (633nm)" package="0603 [SMD]"]
  R1 = Resistor [tolerance=±5% resistance=220 package=THT]
  SG1 = Buzzer 12mm [package=buzzer-12mm-ns]

nets:
  N1: Componente1.D11_PWM/MOSI, SG1.1
  N2: Componente1.D7, R1.Pin_0
  N3: Componente1.GND, LED1.cathode, SG1.2
  N4: LED1.anode, R1.Pin_1
